# Fritzing sketch project-iot (saved by Fritzing 0.9.5d)

parts:
  A1 = Raspberry Pi 5
  M1 = DOIT Esp32 DevKit v1 (30 pins long, 11 pins width) [part_number=ESP32S-PIN30]
  DC1 = DC_DC_XL4016 [package=board_screw]
  M4 = BTS7960
  M5 = BTS7960
  M6 = DC Motor  # not connected
  M7 = DC Motor  # not connected
  S6 = Round Pushbutton
  HC-SR04_Sensor_1 = HC-SR04 Ultrasonic Distance Sensor
  HC-SR04_Sensor_2 = HC-SR04 Ultrasonic Distance Sensor
  M8 = DC Motor
  BAT1 = 12 battery [package=battery]
  BAT2 = 12 battery [package=battery]
  U1 = LM2596 step down module
  U2 = 2-Channel 5v Relay Shield [package=relay-2ch5v10a]
  M10 = DC Motor
  LED1 = LEDs [package=led10mm]
  LED2 = LEDs [package=led10mm]
  U3 = 2-Channel 5v Relay Shield [package=relay-2ch5v10a]
  LED3 = LEDs [package=led10mm]
  LED4 = LEDs [package=led10mm]
  S7 = Round Pushbutton

nets:
  VCC: A1.5V, A1.GPIO2, A1.Fan-5V, M1.VIN, DC1.OUT+, HC-SR04_Sensor_1.VCC, HC-SR04_Sensor_2.VCC, U2.VCC, U3.VCC
  GND: A1.GND, A1.GPIO15, M1.GND, M1.TX2, DC1.OUT-, M4.pin8, M5.pin8, S6.leg0, HC-SR04_Sensor_1.GND, HC-SR04_Sensor_2.GND, U2.GND, U3.GND, S7.leg0
  N1: A1.GPIO14, M1.RX2
  N2: M1.3V3, M4.pin7, M5.pin7
  N3: M1.D15, M1.D33, M4.pin2
  N4: M1.D4, U2.IN2
  N5: M1.D5, U2.IN1
  N6: M1.D18, M4.pin3, M4.pin4
  N7: M1.D19, M5.pin3, M5.pin4
  N8: M1.D21, S7.leg1
  N9: M1.D22, M5.pin1
  N10: M1.D23, M5.pin2
  N11: M1.D34, HC-SR04_Sensor_2.ECHO
  N12: M1.D35, HC-SR04_Sensor_1.ECHO
  N13: M1.D32, M4.pin1
  N14: M1.D25, U3.IN2
  N15: M1.D26, U3.IN1
  N16: M1.D27, HC-SR04_Sensor_2.TRIG
  N17: M1.D14, HC-SR04_Sensor_1.TRIG
  N18: M1.D13, S6.leg1
  N19: DC1.IN+, M4.pin11, M5.pin11, BAT1.+, U1.IN+, U3.K1-On, U3.K2-On
  N20: M4.pin12, M5.pin12, BAT2.-, U1.IN-, U1.OUT-, U2.K1-Off, U2.K2-Off, LED1.C, LED2.C, LED3.C, LED4.C
  N21: M8.pin_2, U2.K1-In, M10.pin_1
  N22: BAT1.-, BAT2.+
  N23: U1.OUT+, U2.K1-On, U2.K2-On
  N24: U2.K2-In, M10.pin_2
  N25: LED1.A, U3.K1-In, LED3.A
  N26: LED2.A, U3.K2-In, LED4.A

custom parts:
  Raspberry Pi 5: The RPi5, a faster version of the awesome Raspberry Pi4B ARM Board with 40 pin gpio.
  DOIT Esp32 DevKit v1 (30 pins long, 11 pins width): The DOIT Esp32 DevKit v1 is one of the development board created by DOIT to evaluate the ESP-WROOM-32 module. It is based on the ESP32 microcontroller that boasts Wifi, Bluetooth, Ethernet and Low Power support all in a single chip. (vanepp) made breadboard work, adjusted pin numbering and labels and reduced size of schematic and cleaned up pcb. This chip is 30pins long (2 x15) and 11 pins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
  BTS7960: BTS7960 43A Peak Power H-Bridge PWM Motor Driver
  12 battery: 12V lead acid type battery, like the Husqvarna YTH2448 12V 35AH battery. This is the mini version 1/4 the size of the actual battery to be closer to typical breadboard parts (around 2in wide rathher than 7in). The pads in pcb are sized to accomidate up to 14ga wire (as these batterys will deliver high currents.)
  LM2596 step down module: LM2596 DC-DC step down power supply module 3 A.
  2-Channel 5v Relay Shield: 2 Channel 5v Relay Shield w. 2x SPD-06VDC-SD-C
